// Digital circuit READ_WRITE_REGISTER_64BIT.dig as structural Verilog
module READ_WRITE_REGISTER_64BIT (
  input  in_1,
  input  in_2,
  input  in_3
);

  wire and_1_out, and_2_out, and_3_out, and_4_out, and_5_out, and_6_out, and_7_out, and_8_out, and_16_out,
       and_23_out, and_24_out, and_31_out, and_32_out, and_39_out, and_40_out, and_47_out, and_48_out,
       and_55_out, and_56_out, and_63_out, and_64_out, and_71_out, and_72_out, not_1_out, not_2_out,
       not_3_out, not_4_out, not_5_out, not_6_out, not_7_out, not_8_out, not_9_out, not_10_out, not_11_out,
       not_12_out, or_1_out, or_2_out, or_3_out, or_4_out, or_5_out, or_6_out, or_7_out, or_8_out, or_9_out,
       or_10_out, or_11_out, or_12_out, or_17_out, or_18_out, or_19_out, or_20_out;

  and and_1 (and_1_out, not_1_out, not_2_out, not_3_out);
  not not_1 (not_1_out, in_1);
  not not_2 (not_2_out, in_2);
  not not_3 (not_3_out, in_3);
  and and_2 (and_2_out, not_4_out, not_5_out, in_3);
  not not_4 (not_4_out, in_1);
  not not_5 (not_5_out, in_2);
  and and_3 (and_3_out, not_6_out, in_2, not_7_out);
  not not_6 (not_6_out, in_1);
  not not_7 (not_7_out, in_3);
  and and_4 (and_4_out, not_8_out, in_2, in_3);
  not not_8 (not_8_out, in_1);
  and and_5 (and_5_out, in_1, not_9_out, not_10_out);
  not not_9 (not_9_out, in_2);
  not not_10 (not_10_out, in_3);
  and and_6 (and_6_out, in_1, not_11_out, in_3);
  not not_11 (not_11_out, in_2);
  and and_7 (and_7_out, in_1, in_2, not_12_out);
  not not_12 (not_12_out, in_3);
  and and_8 (and_8_out, in_1, in_2, in_3);
  // And and_9 has open pins: In_1=open, In_2=and_1_out, out=open
  // And and_10 has open pins: In_1=open, In_2=and_1_out, out=open
  // And and_11 has open pins: In_1=open, In_2=and_1_out, out=open
  // And and_12 has open pins: In_1=open, In_2=and_1_out, out=open
  // And and_13 has open pins: In_1=open, In_2=and_1_out, out=open
  // And and_14 has open pins: In_1=open, In_2=and_1_out, out=open
  // And and_15 has open pins: In_1=open, In_2=and_1_out, out=open
  buf and_16 (and_16_out, and_1_out);  // And open: In_1
  // And and_17 has open pins: In_1=open, In_2=and_2_out, out=open
  // And and_18 has open pins: In_1=open, In_2=and_2_out, out=open
  // And and_19 has open pins: In_1=open, In_2=and_2_out, out=open
  // And and_20 has open pins: In_1=open, In_2=and_2_out, out=open
  // And and_21 has open pins: In_1=open, In_2=and_2_out, out=open
  // And and_22 has open pins: In_1=open, In_2=and_2_out, out=open
  buf and_23 (and_23_out, and_2_out);  // And open: In_1
  buf and_24 (and_24_out, and_2_out);  // And open: In_1
  // And and_25 has open pins: In_1=open, In_2=and_3_out, out=open
  // And and_26 has open pins: In_1=open, In_2=and_3_out, out=open
  // And and_27 has open pins: In_1=open, In_2=and_3_out, out=open
  // And and_28 has open pins: In_1=open, In_2=and_3_out, out=open
  // And and_29 has open pins: In_1=open, In_2=and_3_out, out=open
  // And and_30 has open pins: In_1=open, In_2=and_3_out, out=open
  buf and_31 (and_31_out, and_3_out);  // And open: In_1
  buf and_32 (and_32_out, and_3_out);  // And open: In_1
  // And and_33 has open pins: In_1=open, In_2=and_4_out, out=open
  // And and_34 has open pins: In_1=open, In_2=and_4_out, out=open
  // And and_35 has open pins: In_1=open, In_2=and_4_out, out=open
  // And and_36 has open pins: In_1=open, In_2=and_4_out, out=open
  // And and_37 has open pins: In_1=open, In_2=and_4_out, out=open
  // And and_38 has open pins: In_1=open, In_2=and_4_out, out=open
  buf and_39 (and_39_out, and_4_out);  // And open: In_1
  buf and_40 (and_40_out, and_4_out);  // And open: In_1
  // And and_41 has open pins: In_1=open, In_2=and_5_out, out=open
  // And and_42 has open pins: In_1=open, In_2=and_5_out, out=open
  // And and_43 has open pins: In_1=open, In_2=and_5_out, out=open
  // And and_44 has open pins: In_1=open, In_2=and_5_out, out=open
  // And and_45 has open pins: In_1=open, In_2=and_5_out, out=open
  // And and_46 has open pins: In_1=open, In_2=and_5_out, out=open
  buf and_47 (and_47_out, and_5_out);  // And open: In_1
  buf and_48 (and_48_out, and_5_out);  // And open: In_1
  // And and_49 has open pins: In_1=open, In_2=and_6_out, out=open
  // And and_50 has open pins: In_1=open, In_2=and_6_out, out=open
  // And and_51 has open pins: In_1=open, In_2=and_6_out, out=open
  // And and_52 has open pins: In_1=open, In_2=and_6_out, out=open
  // And and_53 has open pins: In_1=open, In_2=and_6_out, out=open
  // And and_54 has open pins: In_1=open, In_2=and_6_out, out=open
  buf and_55 (and_55_out, and_6_out);  // And open: In_1
  buf and_56 (and_56_out, and_6_out);  // And open: In_1
  // And and_57 has open pins: In_1=open, In_2=and_7_out, out=open
  // And and_58 has open pins: In_1=open, In_2=and_7_out, out=open
  // And and_59 has open pins: In_1=open, In_2=and_7_out, out=open
  // And and_60 has open pins: In_1=open, In_2=and_7_out, out=open
  // And and_61 has open pins: In_1=open, In_2=and_7_out, out=open
  // And and_62 has open pins: In_1=open, In_2=and_7_out, out=open
  buf and_63 (and_63_out, and_7_out);  // And open: In_1
  buf and_64 (and_64_out, and_7_out);  // And open: In_1
  // And and_65 has open pins: In_1=open, In_2=and_8_out, out=open
  // And and_66 has open pins: In_1=open, In_2=and_8_out, out=open
  // And and_67 has open pins: In_1=open, In_2=and_8_out, out=open
  // And and_68 has open pins: In_1=open, In_2=and_8_out, out=open
  // And and_69 has open pins: In_1=open, In_2=and_8_out, out=open
  // And and_70 has open pins: In_1=open, In_2=and_8_out, out=open
  buf and_71 (and_71_out, and_8_out);  // And open: In_1
  buf and_72 (and_72_out, and_8_out);  // And open: In_1
  // Or or_1 has open pins: In_1=open, In_2=open, In_3=open, In_4=open, out=or_1_out
  // Or or_2 has open pins: In_1=open, In_2=open, In_3=open, In_4=open, out=or_2_out
  // Or or_3 has open pins: In_1=open, In_2=open, In_3=open, In_4=open, out=or_3_out
  // Or or_4 has open pins: In_1=open, In_2=open, In_3=open, In_4=open, out=or_4_out
  // Or or_5 has open pins: In_1=open, In_2=open, In_3=open, In_4=open, out=or_5_out
  // Or or_6 has open pins: In_1=open, In_2=open, In_3=open, In_4=open, out=or_6_out
  buf or_7 (or_7_out, or_1_out);  // Or open: In_1, In_2, In_3
  buf or_8 (or_8_out, or_2_out);  // Or open: In_1, In_2, In_3
  buf or_9 (or_9_out, or_3_out);  // Or open: In_1, In_2, In_3
  buf or_10 (or_10_out, or_4_out);  // Or open: In_1, In_2, In_3
  or or_11 (or_11_out, and_47_out, and_55_out, and_63_out, and_71_out);
  or or_12 (or_12_out, and_48_out, and_56_out, and_64_out, and_72_out);
  // Or or_13 has open pins: In_1=open, In_2=or_7_out, out=open
  // Or or_14 has open pins: In_1=open, In_2=or_8_out, out=open
  // Or or_15 has open pins: In_1=open, In_2=or_9_out, out=open
  // Or or_16 has open pins: In_1=open, In_2=or_10_out, out=open
  buf or_17 (or_17_out, or_5_out);  // Or open: In_1, In_2, In_3
  buf or_18 (or_18_out, or_6_out);  // Or open: In_1, In_2, In_3
  or or_19 (or_19_out, and_23_out, and_31_out, and_39_out, or_11_out);
  or or_20 (or_20_out, and_24_out, and_32_out, and_40_out, or_12_out);
  // Or or_21 has open pins: In_1=open, In_2=or_17_out, out=open
  // Or or_22 has open pins: In_1=open, In_2=or_18_out, out=open
  // Or or_23 has open pins: In_1=open, In_2=or_19_out, out=open
  // Or or_24 has open pins: In_1=and_16_out, In_2=or_20_out, out=open
endmodule
